# Fritzing sketch Interactive_Demoscene (saved by Fritzing 0.9.5d)
breadboards: 1

parts:
  Composant1 = Arduino Uno (Rev3)
  Composant2 = Thumb Joystick
  LCD1 = TFT 1.8 inch 160x128 no SD
  R1 = Rotary Potentiometer (Small) [maximum_resistance=100kΩ package=THT]
  R2 = Rotary Potentiometer (Small) [maximum_resistance=100kΩ package=THT]
  R3 = Rotary Potentiometer (Small) [maximum_resistance=100kΩ package=THT]

nets:
  N1: Composant1.A0, Composant2.VERT
  N2: Composant1.A1, Composant2.HORZ
  N3: Composant1.A3, R1.wiper
  N4: Composant1.A4/SDA, R2.wiper
  N5: Composant1.A5/SCL, R3.wiper
  N6: Composant1.D8, LCD1.pin4
  N7: Composant1.D9_PWM, LCD1.pin_5
  N8: Composant1.D10_PWM/SS, LCD1.pin3
  N9: Composant1.D11_PWM/MOSI, LCD1.pin_6
  N10: Composant1.D13/SCK, LCD1.pin_7
  N11: Composant1.D4, Composant2.SEL
  N12: Composant1.3V3, LCD1.pin_1, LCD1.pin_8
  5V: Composant1.5V, Composant2.VCC, R1.leg2, R2.leg2, R3.leg2
  GND: Composant1.GND, Composant2.GND, LCD1.pin2, R1.leg1, R2.leg1, R3.leg1

custom parts:
  TFT 1.8 inch 160x128 no SD: This is a generic 1.8 tft spi lcd display available on ebay and others. The 1.8" display has 128x160 color pixels and in this version pin names in breadboard (unlike the real board) and with no SD interface.
